# Fritzing sketch Sketch Sensores Unidos (saved by Fritzing 0.9.3b)
breadboards: 1

parts:
  Componente2 = InvenSense MPU6050
  microSD1 = MicroSD Card Module
  Componente3 = Bluetooth HC-05 Macho
  Componente1 = Arduino Uno (Rev3)

nets:
  VCC: Componente2.VCC, Componente1.3V3
  GND: Componente2.GND, microSD1.GND, Componente3.GND, Componente1.GND
  N1: Componente2.SCL, Componente1.A5/SCL
  N2: Componente2.SDA, Componente1.A4/SDA
  VCC_2: microSD1.VCC, Componente3.VCC, Componente1.5V
  N3: microSD1.MISO, Componente1.D12/MISO
  N4: microSD1.MOSI, Componente1.D11_PWM/MOSI
  N5: microSD1.SCK, Componente1.D13/SCK
  N6: Componente3.TXD, Componente1.D1/TX
  N7: Componente3.RXD, Componente1.D0/RX
